// Logisim project hw4.circ as structural Verilog: 13 circuits, main circuit main
module _16BitRegister (
  input  [15:0] Input,
  input  CLK,
  input  WE,
  input  RS,
  output [15:0] Output
);

  D_Flip_Flop d_ff_1 (.clk(CLK), .D(Input[0]), .Q(Output[0]), .en(WE), .reset(RS));  // open: Qn, preset
  D_Flip_Flop d_ff_2 (.clk(CLK), .D(Input[1]), .Q(Output[1]), .en(WE), .reset(RS));  // open: Qn, preset
  D_Flip_Flop d_ff_3 (.clk(CLK), .D(Input[2]), .Q(Output[2]), .en(WE), .reset(RS));  // open: Qn, preset
  D_Flip_Flop d_ff_4 (.clk(CLK), .D(Input[3]), .Q(Output[3]), .en(WE), .reset(RS));  // open: Qn, preset
  D_Flip_Flop d_ff_5 (.clk(CLK), .D(Input[4]), .Q(Output[4]), .en(WE), .reset(RS));  // open: Qn, preset
  D_Flip_Flop d_ff_6 (.clk(CLK), .D(Input[5]), .Q(Output[5]), .en(WE), .reset(RS));  // open: Qn, preset
  D_Flip_Flop d_ff_7 (.clk(CLK), .D(Input[6]), .Q(Output[6]), .en(WE), .reset(RS));  // open: Qn, preset
  D_Flip_Flop d_ff_8 (.clk(CLK), .D(Input[7]), .Q(Output[7]), .en(WE), .reset(RS));  // open: Qn, preset
  D_Flip_Flop d_ff_9 (.clk(CLK), .D(Input[8]), .Q(Output[8]), .en(WE), .reset(RS));  // open: Qn, preset
  D_Flip_Flop d_ff_10 (.clk(CLK), .D(Input[9]), .Q(Output[9]), .en(WE), .reset(RS));  // open: Qn, preset
  D_Flip_Flop d_ff_11 (.clk(CLK), .D(Input[10]), .Q(Output[10]), .en(WE), .reset(RS));  // open: Qn, preset
  D_Flip_Flop d_ff_12 (.clk(CLK), .D(Input[11]), .Q(Output[11]), .en(WE), .reset(RS));  // open: Qn, preset
  D_Flip_Flop d_ff_13 (.clk(CLK), .D(Input[12]), .Q(Output[12]), .en(WE), .reset(RS));  // open: Qn, preset
  D_Flip_Flop d_ff_14 (.clk(CLK), .D(Input[13]), .Q(Output[13]), .en(WE), .reset(RS));  // open: Qn, preset
  D_Flip_Flop d_ff_15 (.clk(CLK), .D(Input[14]), .Q(Output[14]), .en(WE), .reset(RS));  // open: Qn, preset
  D_Flip_Flop d_ff_16 (.clk(CLK), .D(Input[15]), .Q(Output[15]), .en(WE), .reset(RS));  // open: Qn, preset
endmodule

module RegisterFile (
  input  reset,
  input  [2:0] ReadReg1,
  input  [2:0] ReadReg2,
  input  [2:0] WriteReg,
  input  [15:0] Data,
  input  RegWriteEnable,
  input  clk,
  output [15:0] ReadData1,
  output [15:0] ReadData2
);

  wire and_1_out, and_2_out, and_3_out, and_4_out, and_5_out, and_6_out, and_7_out, decoder_1_out1,
       decoder_1_out2, decoder_1_out3, decoder_1_out4, decoder_1_out5, decoder_1_out6, decoder_1_out7,
       decoder_2_out0, decoder_2_out1, decoder_2_out2, decoder_2_out3, decoder_2_out4, decoder_2_out5,
       decoder_2_out6, decoder_2_out7, decoder_3_out0, decoder_3_out1, decoder_3_out2, decoder_3_out3,
       decoder_3_out4, decoder_3_out5, decoder_3_out6, decoder_3_out7;
  wire [15:0] n16bitregister_1_output, n16bitregister_2_output, n16bitregister_3_output,
       n16bitregister_4_output, n16bitregister_5_output, n16bitregister_6_output, n16bitregister_7_output,
       n16bitregister_8_output;

  Decoder #(.select(3)) decoder_1 (
    .out1(decoder_1_out1), .out2(decoder_1_out2), .out3(decoder_1_out3), .out4(decoder_1_out4),
    .out5(decoder_1_out5), .out6(decoder_1_out6), .out7(decoder_1_out7), .sel(WriteReg));  // open: out0, en
  and and_1 (and_1_out, decoder_1_out1, RegWriteEnable);
  and and_2 (and_2_out, decoder_1_out2, RegWriteEnable);
  and and_3 (and_3_out, decoder_1_out3, RegWriteEnable);
  and and_4 (and_4_out, decoder_1_out4, RegWriteEnable);
  and and_5 (and_5_out, decoder_1_out5, RegWriteEnable);
  and and_6 (and_6_out, decoder_1_out6, RegWriteEnable);
  and and_7 (and_7_out, decoder_1_out7, RegWriteEnable);
  // Probe on n16bitregister_1_output
  _16BitRegister u_16bitregister_1 (
    .Input({16{1'b0}}), .CLK(clk), .RS(reset), .Output(n16bitregister_1_output));  // open: WE
  // Probe on n16bitregister_2_output
  _16BitRegister u_16bitregister_2 (
    .Input(Data), .CLK(clk), .WE(and_1_out), .RS(reset), .Output(n16bitregister_2_output));
  // Probe on n16bitregister_3_output
  _16BitRegister u_16bitregister_3 (
    .Input(Data), .CLK(clk), .WE(and_2_out), .RS(reset), .Output(n16bitregister_3_output));
  // Probe on n16bitregister_4_output
  _16BitRegister u_16bitregister_4 (
    .Input(Data), .CLK(clk), .WE(and_3_out), .RS(reset), .Output(n16bitregister_4_output));
  // Probe on n16bitregister_5_output
  _16BitRegister u_16bitregister_5 (
    .Input(Data), .CLK(clk), .WE(and_4_out), .RS(reset), .Output(n16bitregister_5_output));
  _16BitRegister u_16bitregister_6 (
    .Input(Data), .CLK(clk), .WE(and_5_out), .RS(reset), .Output(n16bitregister_6_output));
  // Probe on n16bitregister_6_output
  // Probe on n16bitregister_7_output
  _16BitRegister u_16bitregister_7 (
    .Input(Data), .CLK(clk), .WE(and_6_out), .RS(reset), .Output(n16bitregister_7_output));
  // Probe on n16bitregister_8_output
  _16BitRegister u_16bitregister_8 (
    .Input(Data), .CLK(clk), .WE(and_7_out), .RS(reset), .Output(n16bitregister_8_output));
  assign ReadData2 = decoder_2_out0 ? n16bitregister_1_output : 16'bz;  // Controlled_Buffer controlled_buffer_1
  assign ReadData2 = decoder_2_out1 ? n16bitregister_2_output : 16'bz;  // Controlled_Buffer controlled_buffer_2
  assign ReadData2 = decoder_2_out2 ? n16bitregister_3_output : 16'bz;  // Controlled_Buffer controlled_buffer_3
  assign ReadData2 = decoder_2_out3 ? n16bitregister_4_output : 16'bz;  // Controlled_Buffer controlled_buffer_4
  Decoder #(.select(3), .enable("false")) decoder_2 (
    .out0(decoder_2_out0), .out1(decoder_2_out1), .out2(decoder_2_out2), .out3(decoder_2_out3),
    .out4(decoder_2_out4), .out5(decoder_2_out5), .out6(decoder_2_out6), .out7(decoder_2_out7), .sel(ReadReg2));
  assign ReadData1 = decoder_3_out0 ? n16bitregister_1_output : 16'bz;  // Controlled_Buffer controlled_buffer_5
  assign ReadData2 = decoder_2_out4 ? n16bitregister_5_output : 16'bz;  // Controlled_Buffer controlled_buffer_6
  assign ReadData2 = decoder_2_out5 ? n16bitregister_6_output : 16'bz;  // Controlled_Buffer controlled_buffer_7
  assign ReadData2 = decoder_2_out6 ? n16bitregister_7_output : 16'bz;  // Controlled_Buffer controlled_buffer_8
  assign ReadData2 = decoder_2_out7 ? n16bitregister_8_output : 16'bz;  // Controlled_Buffer controlled_buffer_9
  Decoder #(.select(3), .enable("false")) decoder_3 (
    .out0(decoder_3_out0), .out1(decoder_3_out1), .out2(decoder_3_out2), .out3(decoder_3_out3),
    .out4(decoder_3_out4), .out5(decoder_3_out5), .out6(decoder_3_out6), .out7(decoder_3_out7), .sel(ReadReg1));
  assign ReadData1 = decoder_3_out1 ? n16bitregister_2_output : 16'bz;  // Controlled_Buffer controlled_buffer_10
  assign ReadData1 = decoder_3_out2 ? n16bitregister_3_output : 16'bz;  // Controlled_Buffer controlled_buffer_11
  assign ReadData1 = decoder_3_out3 ? n16bitregister_4_output : 16'bz;  // Controlled_Buffer controlled_buffer_12
  assign ReadData1 = decoder_3_out4 ? n16bitregister_5_output : 16'bz;  // Controlled_Buffer controlled_buffer_13
  assign ReadData1 = decoder_3_out5 ? n16bitregister_6_output : 16'bz;  // Controlled_Buffer controlled_buffer_14
  assign ReadData1 = decoder_3_out6 ? n16bitregister_7_output : 16'bz;  // Controlled_Buffer controlled_buffer_15
  assign ReadData1 = decoder_3_out7 ? n16bitregister_8_output : 16'bz;  // Controlled_Buffer controlled_buffer_16

  // Other names for the same wires on the sheet: R1[2:0] = ReadReg1; R2[2:0] = ReadReg2; WE = RegWriteEnable
endmodule

module ALU (
  input  [2:0] ALUop,
  input  [15:0] InputData1_RS,
  input  [15:0] InputData2_RT,
  input  [2:0] shamt,
  output ovf,
  output [15:0] OutputData_RD
);

  wire adder_1_ovf, subtractor_1_ovf;
  wire [15:0] adder_1_result, not_1_out, sll_output, srl_output, subtractor_1_result, xor_1_out;

  adder adder_1 (.A(InputData1_RS), .B(InputData2_RT), .result(adder_1_result), .ovf(adder_1_ovf));
  subtractor subtractor_1 (.A(InputData1_RS), .B(InputData2_RT), .result(subtractor_1_result), .ovf(subtractor_1_ovf));
  assign xor_1_out = InputData1_RS ^ InputData2_RT;  // XOR_Gate xor_1, 16 bits wide
  shiftleft sll (.\input (InputData1_RS), .shamt(shamt), .\output (sll_output));
  shiftright srl (.\input (InputData1_RS), .shamt(shamt), .\output (srl_output));
  assign not_1_out = ~InputData1_RS;  // NOT_Gate not_1, 16 bits wide
  or or_1 (ovf, adder_1_ovf, subtractor_1_ovf);
  Multiplexer #(.select(3), .width(16), .enable("false")) multiplexer_1 (
    .in0(adder_1_result), .in1(subtractor_1_result), .in2(not_1_out), .in3(xor_1_out), .in4(sll_output),
    .in5(srl_output), .out(OutputData_RD), .sel(ALUop));  // open: in6, in7

  // Other names for the same wires on the sheet: OT[2:0] = ALUop; sh[2:0] = shamt
endmodule

module InstructionDecode (
  input  [15:0] instruction,
  output [2:0] shamt,
  output [5:0] immed,
  output [15:0] address,
  output [2:0] RS,
  output [2:0] RT,
  output [2:0] RD,
  output WE,
  output ALUinB,
  output rdst,
  output rwd,
  output DMwe,
  output bne,
  output blt,
  output ioin,
  output ioout,
  output [2:0] ALUop,
  output [1:0] j,
  output jal
);

  wire add, addi, bne_t, I, J_t, j_t_t, jr, \not , not_1_out, not_2_out, not_3_out, not_4_out, not_5_out,
       not_6_out, not_7_out, not_8_out, not_10_out, not_11_out, not_12_out, not_13_out, not_14_out,
       not_15_out, not_16_out, not_17_out, not_18_out, not_19_out, not_20_out, not_21_out, not_22_out,
       not_23_out, not_24_out, not_25_out, not_26_out, not_27_out, not_28_out, not_29_out, not_30_out,
       not_31_out, not_32_out, not_33_out, or_1_out, or_2_out, or_3_out, R, sll, srl, sub, \xor ;

  not not_1 (not_1_out, instruction[12]);
  not not_2 (not_2_out, instruction[13]);
  and u_add (add, not_1_out, not_2_out, not_3_out, not_4_out);
  not not_3 (not_3_out, instruction[14]);
  not not_4 (not_4_out, instruction[15]);
  not not_5 (not_5_out, instruction[13]);
  and u_sub (sub, instruction[12], not_5_out, not_6_out, not_7_out);
  not not_6 (not_6_out, instruction[14]);
  not not_7 (not_7_out, instruction[15]);
  not not_8 (not_8_out, instruction[12]);
  and not_9 (\not , not_8_out, instruction[13], not_10_out, not_11_out);
  not not_10 (not_10_out, instruction[14]);
  not not_11 (not_11_out, instruction[15]);
  and u_xor (\xor , instruction[12], instruction[13], not_12_out, not_13_out);
  not not_12 (not_12_out, instruction[14]);
  not not_13 (not_13_out, instruction[15]);
  not not_14 (not_14_out, instruction[12]);
  not not_15 (not_15_out, instruction[13]);
  and u_sll (sll, not_14_out, not_15_out, instruction[14], not_16_out);
  not not_16 (not_16_out, instruction[15]);
  not not_17 (not_17_out, instruction[13]);
  and u_srl (srl, instruction[12], not_17_out, instruction[14], not_18_out);
  not not_18 (not_18_out, instruction[15]);
  not not_19 (not_19_out, instruction[12]);
  and u_addi (addi, not_19_out, instruction[13], instruction[14], not_20_out);
  not not_20 (not_20_out, instruction[15]);
  and lw (rwd, instruction[12], instruction[13], instruction[14], not_21_out);
  not not_21 (not_21_out, instruction[15]);
  not not_22 (not_22_out, instruction[12]);
  not not_23 (not_23_out, instruction[13]);
  and sw (DMwe, not_22_out, not_23_out, not_24_out, instruction[15]);
  not not_24 (not_24_out, instruction[14]);
  not not_25 (not_25_out, instruction[13]);
  and u_bne (bne_t, instruction[12], not_25_out, not_26_out, instruction[15]);
  not not_26 (not_26_out, instruction[14]);
  not not_27 (not_27_out, instruction[12]);
  and u_blt (blt, not_27_out, instruction[13], not_28_out, instruction[15]);
  not not_28 (not_28_out, instruction[14]);
  and u_j (j_t_t, instruction[12], instruction[13], not_29_out, instruction[15]);
  not not_29 (not_29_out, instruction[14]);
  not not_30 (not_30_out, instruction[12]);
  not not_31 (not_31_out, instruction[13]);
  and u_jr (jr, not_30_out, not_31_out, instruction[14], instruction[15]);
  not not_32 (not_32_out, instruction[13]);
  and u_jal (jal, instruction[12], not_32_out, instruction[14], instruction[15]);
  not not_33 (not_33_out, instruction[12]);
  and \input  (ioin, not_33_out, instruction[13], instruction[14], instruction[15]);
  and \output  (ioout, instruction[12], instruction[13], instruction[14], instruction[15]);
  assign immed = I ? instruction[5:0] : 6'bz;  // Controlled_Buffer controlled_buffer_1
  or R_Type (R, add, sub, \not , jr, \xor , sll, srl);
  or I_Type (I, addi, rwd, DMwe, bne_t, blt, ioin, ioout);
  or J_Type (J_t, j_t_t, jal);
  assign shamt = R ? instruction[2:0] : 3'bz;  // Controlled_Buffer controlled_buffer_2
  assign RS = or_1_out ? instruction[11:9] : 3'bz;  // Controlled_Buffer controlled_buffer_3
  or or_1 (or_1_out, R, I);
  assign RT = or_2_out ? instruction[8:6] : 3'bz;  // Controlled_Buffer controlled_buffer_4
  or or_2 (or_2_out, R, I);
  assign RD = R ? instruction[5:3] : 3'bz;  // Controlled_Buffer controlled_buffer_5
  or or_3 (or_3_out, sub, bne_t, blt);
  or or_4 (ALUop[1], \not , \xor );
  or or_5 (ALUop[2], sll, srl);
  or or_6 (ALUop[0], or_3_out, srl, \xor );
  or or_7 (j[0], j_t_t, jal);
  or or_8 (j[1], jr, jal);
  or or_9 (WE, add, sub, \not , \xor , sll, srl, addi, rwd, jal, ioin);
  or or_10 (ALUinB, addi, rwd, DMwe);
  or or_11 (rdst, addi, ioin, rwd);
  or or_12 (bne, bne_t, blt);
  assign address = J_t ? {4'b0000, instruction[11:0]} : 16'bz;  // Controlled_Buffer controlled_buffer_6

  // Other names for the same wires on the sheet: _0 = instruction[0]; _1 = instruction[1]; _2 = instruction[2];
  //   _3 = instruction[3]; _4 = instruction[4]; _5 = instruction[5]; _6 = instruction[6]; _7 = instruction[7];
  //   _8 = instruction[8]; _9 = instruction[9]; _10 = instruction[10]; _11 = instruction[11]; input = ioin; lw = rwd;
  //   output = ioout; sw = DMwe
endmodule

module SignExtender (
  input  [5:0] \input ,
  output [15:0] \output 
);


  assign \output  = {{11{\input [5]}}, \input [4:0]};

  // Other names for the same wires on the sheet: sign = \input [5]
endmodule

module onebit (
  input  Cin,
  input  A,
  input  B,
  output sum,
  output cout
);

  wire and_1_out, and_2_out, xor_1_out;

  and and_1 (and_1_out, B, A);
  or or_1 (cout, and_1_out, and_2_out);
  xor xor_1 (xor_1_out, A, B);
  and and_2 (and_2_out, xor_1_out, Cin);
  xor xor_2 (sum, Cin, xor_1_out);
endmodule

module adder (
  input  [15:0] A,
  input  [15:0] B,
  output [15:0] result,
  output ovf
);

  wire onebit_1_cout, onebit_2_cout, onebit_3_cout, onebit_4_cout, onebit_5_cout, onebit_6_cout,
       onebit_7_cout, onebit_8_cout, onebit_9_cout, onebit_10_cout, onebit_11_cout, onebit_12_cout,
       onebit_13_cout, onebit_14_cout, onebit_15_cout, onebit_16_cout;

  onebit onebit_1 (.A(A[0]), .B(B[0]), .Cin(1'b0), .cout(onebit_1_cout), .sum(result[0]));
  onebit onebit_2 (.A(A[1]), .B(B[1]), .Cin(onebit_1_cout), .cout(onebit_2_cout), .sum(result[1]));
  onebit onebit_3 (.A(A[2]), .B(B[2]), .Cin(onebit_2_cout), .cout(onebit_3_cout), .sum(result[2]));
  onebit onebit_4 (.A(A[3]), .B(B[3]), .Cin(onebit_3_cout), .cout(onebit_4_cout), .sum(result[3]));
  onebit onebit_5 (.A(A[4]), .B(B[4]), .Cin(onebit_4_cout), .cout(onebit_5_cout), .sum(result[4]));
  onebit onebit_6 (.A(A[5]), .B(B[5]), .Cin(onebit_5_cout), .cout(onebit_6_cout), .sum(result[5]));
  onebit onebit_7 (.A(A[6]), .B(B[6]), .Cin(onebit_6_cout), .cout(onebit_7_cout), .sum(result[6]));
  onebit onebit_8 (.A(A[7]), .B(B[7]), .Cin(onebit_7_cout), .cout(onebit_8_cout), .sum(result[7]));
  onebit onebit_9 (.A(A[8]), .B(B[8]), .Cin(onebit_8_cout), .cout(onebit_9_cout), .sum(result[8]));
  onebit onebit_10 (.A(A[9]), .B(B[9]), .Cin(onebit_9_cout), .cout(onebit_10_cout), .sum(result[9]));
  onebit onebit_11 (.A(A[10]), .B(B[10]), .Cin(onebit_10_cout), .cout(onebit_11_cout), .sum(result[10]));
  onebit onebit_12 (.A(A[11]), .B(B[11]), .Cin(onebit_11_cout), .cout(onebit_12_cout), .sum(result[11]));
  onebit onebit_13 (.A(A[12]), .B(B[12]), .Cin(onebit_12_cout), .cout(onebit_13_cout), .sum(result[12]));
  onebit onebit_14 (.A(A[13]), .B(B[13]), .Cin(onebit_13_cout), .cout(onebit_14_cout), .sum(result[13]));
  onebit onebit_15 (.A(A[14]), .B(B[14]), .Cin(onebit_14_cout), .cout(onebit_15_cout), .sum(result[14]));
  onebit onebit_16 (.A(A[15]), .B(B[15]), .Cin(onebit_15_cout), .cout(onebit_16_cout), .sum(result[15]));
  xor xor_1 (ovf, onebit_15_cout, onebit_16_cout);
endmodule

module subtractor (
  input  [15:0] A,
  input  [15:0] B,
  output [15:0] result,
  output ovf
);

  wire onebit_1_cout, onebit_2_cout, onebit_3_cout, onebit_4_cout, onebit_5_cout, onebit_6_cout,
       onebit_7_cout, onebit_8_cout, onebit_9_cout, onebit_10_cout, onebit_11_cout, onebit_12_cout,
       onebit_13_cout, onebit_14_cout, onebit_15_cout, onebit_16_cout, xor_1_out, xor_2_out, xor_3_out,
       xor_4_out, xor_5_out, xor_6_out, xor_7_out, xor_8_out, xor_9_out, xor_10_out, xor_11_out, xor_12_out,
       xor_13_out, xor_14_out, xor_15_out, xor_16_out;

  xor xor_1 (xor_1_out, 1'b1, B[0]);
  xor xor_2 (xor_2_out, 1'b1, B[1]);
  xor xor_3 (xor_3_out, 1'b1, B[2]);
  xor xor_4 (xor_4_out, 1'b1, B[3]);
  xor xor_5 (xor_5_out, 1'b1, B[4]);
  xor xor_6 (xor_6_out, 1'b1, B[5]);
  xor xor_7 (xor_7_out, 1'b1, B[6]);
  xor xor_8 (xor_8_out, 1'b1, B[7]);
  xor xor_9 (xor_9_out, 1'b1, B[8]);
  xor xor_10 (xor_10_out, 1'b1, B[9]);
  xor xor_11 (xor_11_out, 1'b1, B[10]);
  xor xor_12 (xor_12_out, 1'b1, B[11]);
  xor xor_13 (xor_13_out, 1'b1, B[12]);
  xor xor_14 (xor_14_out, 1'b1, B[13]);
  xor xor_15 (xor_15_out, 1'b1, B[14]);
  xor xor_16 (xor_16_out, 1'b1, B[15]);
  onebit onebit_1 (.A(A[0]), .B(xor_1_out), .Cin(1'b1), .cout(onebit_1_cout), .sum(result[0]));
  onebit onebit_2 (.A(A[1]), .B(xor_2_out), .Cin(onebit_1_cout), .cout(onebit_2_cout), .sum(result[1]));
  onebit onebit_3 (.A(A[2]), .B(xor_3_out), .Cin(onebit_2_cout), .cout(onebit_3_cout), .sum(result[2]));
  onebit onebit_4 (.A(A[3]), .B(xor_4_out), .Cin(onebit_3_cout), .cout(onebit_4_cout), .sum(result[3]));
  onebit onebit_5 (.A(A[4]), .B(xor_5_out), .Cin(onebit_4_cout), .cout(onebit_5_cout), .sum(result[4]));
  onebit onebit_6 (.A(A[5]), .B(xor_6_out), .Cin(onebit_5_cout), .cout(onebit_6_cout), .sum(result[5]));
  onebit onebit_7 (.A(A[6]), .B(xor_7_out), .Cin(onebit_6_cout), .cout(onebit_7_cout), .sum(result[6]));
  onebit onebit_8 (.A(A[7]), .B(xor_8_out), .Cin(onebit_7_cout), .cout(onebit_8_cout), .sum(result[7]));
  onebit onebit_9 (.A(A[8]), .B(xor_9_out), .Cin(onebit_8_cout), .cout(onebit_9_cout), .sum(result[8]));
  onebit onebit_10 (.A(A[9]), .B(xor_10_out), .Cin(onebit_9_cout), .cout(onebit_10_cout), .sum(result[9]));
  onebit onebit_11 (.A(A[10]), .B(xor_11_out), .Cin(onebit_10_cout), .cout(onebit_11_cout), .sum(result[10]));
  onebit onebit_12 (.A(A[11]), .B(xor_12_out), .Cin(onebit_11_cout), .cout(onebit_12_cout), .sum(result[11]));
  onebit onebit_13 (.A(A[12]), .B(xor_13_out), .Cin(onebit_12_cout), .cout(onebit_13_cout), .sum(result[12]));
  onebit onebit_14 (.A(A[13]), .B(xor_14_out), .Cin(onebit_13_cout), .cout(onebit_14_cout), .sum(result[13]));
  onebit onebit_15 (.A(A[14]), .B(xor_15_out), .Cin(onebit_14_cout), .cout(onebit_15_cout), .sum(result[14]));
  onebit onebit_16 (.A(A[15]), .B(xor_16_out), .Cin(onebit_15_cout), .cout(onebit_16_cout), .sum(result[15]));
  xor xor_17 (ovf, onebit_15_cout, onebit_16_cout);
endmodule

module shiftright (
  input  [15:0] \input ,
  input  [2:0] shamt,
  output [15:0] \output 
);

  wire multiplexer_1_out, multiplexer_2_out, multiplexer_3_out, multiplexer_4_out, multiplexer_5_out,
       multiplexer_6_out, multiplexer_7_out, multiplexer_8_out, multiplexer_9_out, multiplexer_10_out,
       multiplexer_11_out, multiplexer_12_out, multiplexer_13_out, multiplexer_14_out, multiplexer_15_out,
       multiplexer_16_out, multiplexer_17_out, multiplexer_18_out, multiplexer_19_out, multiplexer_20_out,
       multiplexer_21_out, multiplexer_22_out, multiplexer_23_out, multiplexer_24_out, multiplexer_25_out,
       multiplexer_26_out, multiplexer_27_out, multiplexer_28_out, multiplexer_29_out, multiplexer_30_out,
       multiplexer_31_out, multiplexer_32_out;

  Multiplexer #(.enable("false")) multiplexer_1 (
    .in0(\input [0]), .in1(\input [1]), .out(multiplexer_1_out), .sel(shamt[0]));
  Multiplexer #(.enable("false")) multiplexer_2 (
    .in0(\input [1]), .in1(\input [2]), .out(multiplexer_2_out), .sel(shamt[0]));
  Multiplexer #(.enable("false")) multiplexer_3 (
    .in0(\input [2]), .in1(\input [3]), .out(multiplexer_3_out), .sel(shamt[0]));
  Multiplexer #(.enable("false")) multiplexer_4 (
    .in0(\input [3]), .in1(\input [4]), .out(multiplexer_4_out), .sel(shamt[0]));
  Multiplexer #(.enable("false")) multiplexer_5 (
    .in0(\input [4]), .in1(\input [5]), .out(multiplexer_5_out), .sel(shamt[0]));
  Multiplexer #(.enable("false")) multiplexer_6 (
    .in0(\input [5]), .in1(\input [6]), .out(multiplexer_6_out), .sel(shamt[0]));
  Multiplexer #(.enable("false")) multiplexer_7 (
    .in0(\input [6]), .in1(\input [7]), .out(multiplexer_7_out), .sel(shamt[0]));
  Multiplexer #(.enable("false")) multiplexer_8 (
    .in0(\input [7]), .in1(\input [8]), .out(multiplexer_8_out), .sel(shamt[0]));
  Multiplexer #(.enable("false")) multiplexer_9 (
    .in0(\input [8]), .in1(\input [9]), .out(multiplexer_9_out), .sel(shamt[0]));
  Multiplexer #(.enable("false")) multiplexer_10 (
    .in0(\input [9]), .in1(\input [10]), .out(multiplexer_10_out), .sel(shamt[0]));
  Multiplexer #(.enable("false")) multiplexer_11 (
    .in0(\input [10]), .in1(\input [11]), .out(multiplexer_11_out), .sel(shamt[0]));
  Multiplexer #(.enable("false")) multiplexer_12 (
    .in0(\input [11]), .in1(\input [12]), .out(multiplexer_12_out), .sel(shamt[0]));
  Multiplexer #(.enable("false")) multiplexer_13 (
    .in0(\input [12]), .in1(\input [13]), .out(multiplexer_13_out), .sel(shamt[0]));
  Multiplexer #(.enable("false")) multiplexer_14 (
    .in0(\input [13]), .in1(\input [14]), .out(multiplexer_14_out), .sel(shamt[0]));
  Multiplexer #(.enable("false")) multiplexer_15 (
    .in0(\input [14]), .in1(\input [15]), .out(multiplexer_15_out), .sel(shamt[0]));
  Multiplexer #(.enable("false")) multiplexer_16 (
    .in0(\input [15]), .in1(1'b0), .out(multiplexer_16_out), .sel(shamt[0]));
  Multiplexer #(.enable("false")) multiplexer_17 (
    .in0(multiplexer_1_out), .in1(multiplexer_3_out), .out(multiplexer_17_out), .sel(shamt[1]));
  Multiplexer #(.enable("false")) multiplexer_18 (
    .in0(multiplexer_2_out), .in1(multiplexer_4_out), .out(multiplexer_18_out), .sel(shamt[1]));
  Multiplexer #(.enable("false")) multiplexer_19 (
    .in0(multiplexer_3_out), .in1(multiplexer_5_out), .out(multiplexer_19_out), .sel(shamt[1]));
  Multiplexer #(.enable("false")) multiplexer_20 (
    .in0(multiplexer_4_out), .in1(multiplexer_6_out), .out(multiplexer_20_out), .sel(shamt[1]));
  Multiplexer #(.enable("false")) multiplexer_21 (
    .in0(multiplexer_5_out), .in1(multiplexer_7_out), .out(multiplexer_21_out), .sel(shamt[1]));
  Multiplexer #(.enable("false")) multiplexer_22 (
    .in0(multiplexer_6_out), .in1(multiplexer_8_out), .out(multiplexer_22_out), .sel(shamt[1]));
  Multiplexer #(.enable("false")) multiplexer_23 (
    .in0(multiplexer_7_out), .in1(multiplexer_9_out), .out(multiplexer_23_out), .sel(shamt[1]));
  Multiplexer #(.enable("false")) multiplexer_24 (
    .in0(multiplexer_8_out), .in1(multiplexer_10_out), .out(multiplexer_24_out), .sel(shamt[1]));
  Multiplexer #(.enable("false")) multiplexer_25 (
    .in0(multiplexer_9_out), .in1(multiplexer_11_out), .out(multiplexer_25_out), .sel(shamt[1]));
  Multiplexer #(.enable("false")) multiplexer_26 (
    .in0(multiplexer_10_out), .in1(multiplexer_12_out), .out(multiplexer_26_out), .sel(shamt[1]));
  Multiplexer #(.enable("false")) multiplexer_27 (
    .in0(multiplexer_11_out), .in1(multiplexer_13_out), .out(multiplexer_27_out), .sel(shamt[1]));
  Multiplexer #(.enable("false")) multiplexer_28 (
    .in0(multiplexer_12_out), .in1(multiplexer_14_out), .out(multiplexer_28_out), .sel(shamt[1]));
  Multiplexer #(.enable("false")) multiplexer_29 (
    .in0(multiplexer_13_out), .in1(multiplexer_15_out), .out(multiplexer_29_out), .sel(shamt[1]));
  Multiplexer #(.enable("false")) multiplexer_30 (
    .in0(multiplexer_14_out), .in1(multiplexer_16_out), .out(multiplexer_30_out), .sel(shamt[1]));
  Multiplexer #(.enable("false")) multiplexer_31 (
    .in0(multiplexer_15_out), .in1(1'b0), .out(multiplexer_31_out), .sel(shamt[1]));
  Multiplexer #(.enable("false")) multiplexer_32 (
    .in0(multiplexer_16_out), .in1(1'b0), .out(multiplexer_32_out), .sel(shamt[1]));
  Multiplexer #(.enable("false")) multiplexer_33 (
    .in0(multiplexer_17_out), .in1(multiplexer_21_out), .out(\output [0]), .sel(shamt[2]));
  Multiplexer #(.enable("false")) multiplexer_34 (
    .in0(multiplexer_18_out), .in1(multiplexer_22_out), .out(\output [1]), .sel(shamt[2]));
  Multiplexer #(.enable("false")) multiplexer_35 (
    .in0(multiplexer_19_out), .in1(multiplexer_23_out), .out(\output [2]), .sel(shamt[2]));
  Multiplexer #(.enable("false")) multiplexer_36 (
    .in0(multiplexer_20_out), .in1(multiplexer_24_out), .out(\output [3]), .sel(shamt[2]));
  Multiplexer #(.enable("false")) multiplexer_37 (
    .in0(multiplexer_21_out), .in1(multiplexer_25_out), .out(\output [4]), .sel(shamt[2]));
  Multiplexer #(.enable("false")) multiplexer_38 (
    .in0(multiplexer_22_out), .in1(multiplexer_26_out), .out(\output [5]), .sel(shamt[2]));
  Multiplexer #(.enable("false")) multiplexer_39 (
    .in0(multiplexer_23_out), .in1(multiplexer_27_out), .out(\output [6]), .sel(shamt[2]));
  Multiplexer #(.enable("false")) multiplexer_40 (
    .in0(multiplexer_24_out), .in1(multiplexer_28_out), .out(\output [7]), .sel(shamt[2]));
  Multiplexer #(.enable("false")) multiplexer_41 (
    .in0(multiplexer_25_out), .in1(multiplexer_29_out), .out(\output [8]), .sel(shamt[2]));
  Multiplexer #(.enable("false")) multiplexer_42 (
    .in0(multiplexer_26_out), .in1(multiplexer_30_out), .out(\output [9]), .sel(shamt[2]));
  Multiplexer #(.enable("false")) multiplexer_43 (
    .in0(multiplexer_27_out), .in1(multiplexer_31_out), .out(\output [10]), .sel(shamt[2]));
  Multiplexer #(.enable("false")) multiplexer_44 (
    .in0(multiplexer_28_out), .in1(multiplexer_32_out), .out(\output [11]), .sel(shamt[2]));
  Multiplexer #(.enable("false")) multiplexer_45 (
    .in0(multiplexer_29_out), .in1(1'b0), .out(\output [12]), .sel(shamt[2]));
  Multiplexer #(.enable("false")) multiplexer_46 (
    .in0(multiplexer_30_out), .in1(1'b0), .out(\output [13]), .sel(shamt[2]));
  Multiplexer #(.enable("false")) multiplexer_47 (
    .in0(multiplexer_31_out), .in1(1'b0), .out(\output [14]), .sel(shamt[2]));
  Multiplexer #(.enable("false")) multiplexer_48 (
    .in0(multiplexer_32_out), .in1(1'b0), .out(\output [15]), .sel(shamt[2]));

  // Other names for the same wires on the sheet: sh[2:0] = shamt
endmodule

module shiftleft (
  input  [15:0] \input ,
  input  [2:0] shamt,
  output [15:0] \output 
);

  wire multiplexer_1_out, multiplexer_2_out, multiplexer_3_out, multiplexer_4_out, multiplexer_5_out,
       multiplexer_6_out, multiplexer_7_out, multiplexer_8_out, multiplexer_9_out, multiplexer_10_out,
       multiplexer_11_out, multiplexer_12_out, multiplexer_13_out, multiplexer_14_out, multiplexer_15_out,
       multiplexer_16_out, multiplexer_17_out, multiplexer_18_out, multiplexer_19_out, multiplexer_20_out,
       multiplexer_21_out, multiplexer_22_out, multiplexer_23_out, multiplexer_24_out, multiplexer_25_out,
       multiplexer_26_out, multiplexer_27_out, multiplexer_28_out, multiplexer_29_out, multiplexer_30_out,
       multiplexer_31_out, multiplexer_32_out;

  Multiplexer #(.enable("false")) multiplexer_1 (.in0(\input [0]), .in1(1'b0), .out(multiplexer_1_out), .sel(shamt[0]));
  Multiplexer #(.enable("false")) multiplexer_2 (
    .in0(\input [1]), .in1(\input [0]), .out(multiplexer_2_out), .sel(shamt[0]));
  Multiplexer #(.enable("false")) multiplexer_3 (
    .in0(\input [2]), .in1(\input [1]), .out(multiplexer_3_out), .sel(shamt[0]));
  Multiplexer #(.enable("false")) multiplexer_4 (
    .in0(\input [3]), .in1(\input [2]), .out(multiplexer_4_out), .sel(shamt[0]));
  Multiplexer #(.enable("false")) multiplexer_5 (
    .in0(\input [4]), .in1(\input [3]), .out(multiplexer_5_out), .sel(shamt[0]));
  Multiplexer #(.enable("false")) multiplexer_6 (
    .in0(\input [5]), .in1(\input [4]), .out(multiplexer_6_out), .sel(shamt[0]));
  Multiplexer #(.enable("false")) multiplexer_7 (
    .in0(\input [6]), .in1(\input [5]), .out(multiplexer_7_out), .sel(shamt[0]));
  Multiplexer #(.enable("false")) multiplexer_8 (
    .in0(\input [7]), .in1(\input [6]), .out(multiplexer_8_out), .sel(shamt[0]));
  Multiplexer #(.enable("false")) multiplexer_9 (
    .in0(\input [8]), .in1(\input [7]), .out(multiplexer_9_out), .sel(shamt[0]));
  Multiplexer #(.enable("false")) multiplexer_10 (
    .in0(\input [9]), .in1(\input [8]), .out(multiplexer_10_out), .sel(shamt[0]));
  Multiplexer #(.enable("false")) multiplexer_11 (
    .in0(\input [10]), .in1(\input [9]), .out(multiplexer_11_out), .sel(shamt[0]));
  Multiplexer #(.enable("false")) multiplexer_12 (
    .in0(\input [11]), .in1(\input [10]), .out(multiplexer_12_out), .sel(shamt[0]));
  Multiplexer #(.enable("false")) multiplexer_13 (
    .in0(\input [12]), .in1(\input [11]), .out(multiplexer_13_out), .sel(shamt[0]));
  Multiplexer #(.enable("false")) multiplexer_14 (
    .in0(\input [13]), .in1(\input [12]), .out(multiplexer_14_out), .sel(shamt[0]));
  Multiplexer #(.enable("false")) multiplexer_15 (
    .in0(\input [14]), .in1(\input [13]), .out(multiplexer_15_out), .sel(shamt[0]));
  Multiplexer #(.enable("false")) multiplexer_16 (
    .in0(\input [15]), .in1(\input [14]), .out(multiplexer_16_out), .sel(shamt[0]));
  Multiplexer #(.enable("false")) multiplexer_17 (
    .in0(multiplexer_1_out), .in1(1'b0), .out(multiplexer_17_out), .sel(shamt[1]));
  Multiplexer #(.enable("false")) multiplexer_18 (
    .in0(multiplexer_2_out), .in1(1'b0), .out(multiplexer_18_out), .sel(shamt[1]));
  Multiplexer #(.enable("false")) multiplexer_19 (
    .in0(multiplexer_3_out), .in1(multiplexer_1_out), .out(multiplexer_19_out), .sel(shamt[1]));
  Multiplexer #(.enable("false")) multiplexer_20 (
    .in0(multiplexer_4_out), .in1(multiplexer_2_out), .out(multiplexer_20_out), .sel(shamt[1]));
  Multiplexer #(.enable("false")) multiplexer_21 (
    .in0(multiplexer_5_out), .in1(multiplexer_3_out), .out(multiplexer_21_out), .sel(shamt[1]));
  Multiplexer #(.enable("false")) multiplexer_22 (
    .in0(multiplexer_6_out), .in1(multiplexer_4_out), .out(multiplexer_22_out), .sel(shamt[1]));
  Multiplexer #(.enable("false")) multiplexer_23 (
    .in0(multiplexer_7_out), .in1(multiplexer_5_out), .out(multiplexer_23_out), .sel(shamt[1]));
  Multiplexer #(.enable("false")) multiplexer_24 (
    .in0(multiplexer_8_out), .in1(multiplexer_6_out), .out(multiplexer_24_out), .sel(shamt[1]));
  Multiplexer #(.enable("false")) multiplexer_25 (
    .in0(multiplexer_9_out), .in1(multiplexer_7_out), .out(multiplexer_25_out), .sel(shamt[1]));
  Multiplexer #(.enable("false")) multiplexer_26 (
    .in0(multiplexer_10_out), .in1(multiplexer_8_out), .out(multiplexer_26_out), .sel(shamt[1]));
  Multiplexer #(.enable("false")) multiplexer_27 (
    .in0(multiplexer_11_out), .in1(multiplexer_9_out), .out(multiplexer_27_out), .sel(shamt[1]));
  Multiplexer #(.enable("false")) multiplexer_28 (
    .in0(multiplexer_12_out), .in1(multiplexer_10_out), .out(multiplexer_28_out), .sel(shamt[1]));
  Multiplexer #(.enable("false")) multiplexer_29 (
    .in0(multiplexer_13_out), .in1(multiplexer_11_out), .out(multiplexer_29_out), .sel(shamt[1]));
  Multiplexer #(.enable("false")) multiplexer_30 (
    .in0(multiplexer_14_out), .in1(multiplexer_12_out), .out(multiplexer_30_out), .sel(shamt[1]));
  Multiplexer #(.enable("false")) multiplexer_31 (
    .in0(multiplexer_15_out), .in1(multiplexer_13_out), .out(multiplexer_31_out), .sel(shamt[1]));
  Multiplexer #(.enable("false")) multiplexer_32 (
    .in0(multiplexer_16_out), .in1(multiplexer_14_out), .out(multiplexer_32_out), .sel(shamt[1]));
  Multiplexer #(.enable("false")) multiplexer_33 (
    .in0(multiplexer_17_out), .in1(1'b0), .out(\output [0]), .sel(shamt[2]));
  Multiplexer #(.enable("false")) multiplexer_34 (
    .in0(multiplexer_18_out), .in1(1'b0), .out(\output [1]), .sel(shamt[2]));
  Multiplexer #(.enable("false")) multiplexer_35 (
    .in0(multiplexer_19_out), .in1(1'b0), .out(\output [2]), .sel(shamt[2]));
  Multiplexer #(.enable("false")) multiplexer_36 (
    .in0(multiplexer_20_out), .in1(1'b0), .out(\output [3]), .sel(shamt[2]));
  Multiplexer #(.enable("false")) multiplexer_37 (
    .in0(multiplexer_21_out), .in1(multiplexer_17_out), .out(\output [4]), .sel(shamt[2]));
  Multiplexer #(.enable("false")) multiplexer_38 (
    .in0(multiplexer_22_out), .in1(multiplexer_18_out), .out(\output [5]), .sel(shamt[2]));
  Multiplexer #(.enable("false")) multiplexer_39 (
    .in0(multiplexer_23_out), .in1(multiplexer_19_out), .out(\output [6]), .sel(shamt[2]));
  Multiplexer #(.enable("false")) multiplexer_40 (
    .in0(multiplexer_24_out), .in1(multiplexer_20_out), .out(\output [7]), .sel(shamt[2]));
  Multiplexer #(.enable("false")) multiplexer_41 (
    .in0(multiplexer_25_out), .in1(multiplexer_21_out), .out(\output [8]), .sel(shamt[2]));
  Multiplexer #(.enable("false")) multiplexer_42 (
    .in0(multiplexer_26_out), .in1(multiplexer_22_out), .out(\output [9]), .sel(shamt[2]));
  Multiplexer #(.enable("false")) multiplexer_43 (
    .in0(multiplexer_27_out), .in1(multiplexer_23_out), .out(\output [10]), .sel(shamt[2]));
  Multiplexer #(.enable("false")) multiplexer_44 (
    .in0(multiplexer_28_out), .in1(multiplexer_24_out), .out(\output [11]), .sel(shamt[2]));
  Multiplexer #(.enable("false")) multiplexer_45 (
    .in0(multiplexer_29_out), .in1(multiplexer_25_out), .out(\output [12]), .sel(shamt[2]));
  Multiplexer #(.enable("false")) multiplexer_46 (
    .in0(multiplexer_30_out), .in1(multiplexer_26_out), .out(\output [13]), .sel(shamt[2]));
  Multiplexer #(.enable("false")) multiplexer_47 (
    .in0(multiplexer_31_out), .in1(multiplexer_27_out), .out(\output [14]), .sel(shamt[2]));
  Multiplexer #(.enable("false")) multiplexer_48 (
    .in0(multiplexer_32_out), .in1(multiplexer_28_out), .out(\output [15]), .sel(shamt[2]));

  // Other names for the same wires on the sheet: sh[2:0] = shamt
endmodule

module main (
  input  reset
);

  wire ALUinB, and_1_out, blt, bne, clk, DMwe, ioin, ioout, jal, keyboard_1_avail, not_1_out, not_2_out,
       not_3_out, Rdst, Rwd, WE, zero_1_out_3;
  wire [1:0] jump;
  wire [2:0] ALUop, multiplexer_2_out, multiplexer_3_out, rd, rs, rt, shamt;
  wire [5:0] immed;
  wire [6:0] keyboard_1_data;
  wire [15:0] adder_1_result, address, ALU_outputdata_rd, increment_result, instruction, key,
       multiplexer_1_out, multiplexer_4_out, multiplexer_5_out, multiplexer_6_out, multiplexer_7_out,
       multiplexer_8_out, PC_output, ram_1_data, registerfile_1_readdata2, S, SignExtender_output;

  adder increment (.A(16'h1), .B(PC_output), .result(increment_result));  // open: ovf
  _16BitRegister PC (.Input(multiplexer_7_out), .CLK(clk), .WE(1'b1), .RS(reset), .Output(PC_output));
  Clock clock_1 (.out(clk));
  InstructionDecode instructiondecode_1 (
    .instruction(instruction), .shamt(shamt), .immed(immed), .address(address), .RS(rs), .RT(rt), .RD(rd),
    .WE(WE), .ALUinB(ALUinB), .rdst(Rdst), .rwd(Rwd), .DMwe(DMwe), .bne(bne), .blt(blt), .ioin(ioin),
    .ioout(ioout), .ALUop(ALUop), .j(jump), .jal(jal));
  ROM #(.addrWidth(16), .dataWidth(16)) rom_1 (.addr(PC_output), .data(instruction));  // open: sel
  Multiplexer #(.width(16), .enable("false")) multiplexer_1 (
    .in0(multiplexer_4_out), .in1(key), .out(multiplexer_1_out), .sel(ioin));
  Multiplexer #(.width(3), .enable("false")) multiplexer_2 (.in0(rd), .in1(rt), .out(multiplexer_2_out), .sel(Rdst));
  Multiplexer #(.width(3), .enable("false")) multiplexer_3 (
    .in0(multiplexer_2_out), .in1(3'b111), .out(multiplexer_3_out), .sel(jal));
  Multiplexer #(.width(16), .enable("false")) multiplexer_4 (
    .in0(multiplexer_8_out), .in1(increment_result), .out(multiplexer_4_out), .sel(jal));
  not not_1 (not_1_out, clk);
  RegisterFile registerfile_1 (
    .reset(reset), .ReadReg1(rs), .ReadReg2(rt), .WriteReg(multiplexer_3_out), .Data(multiplexer_1_out),
    .RegWriteEnable(WE), .clk(not_1_out), .ReadData1(S), .ReadData2(registerfile_1_readdata2));
  SignExtender SignExtender (.\input (immed), .\output (SignExtender_output));
  not not_2 (not_2_out, clk);
  Multiplexer #(.width(16), .enable("false")) multiplexer_5 (
    .in0(registerfile_1_readdata2), .in1(SignExtender_output), .out(multiplexer_5_out), .sel(ALUinB));
  TTY #(.rows(13), .cols(80)) tty_1 (.data(S[6:0]), .clk(not_2_out), .we(ioout), .clr(reset));
  adder adder_1 (.A(increment_result), .B(SignExtender_output), .result(adder_1_result));  // open: ovf
  zero zero_1 (.\input (ALU_outputdata_rd), .blt(blt), .out_3(zero_1_out_3));
  ALU ALU (
    .ALUop(ALUop), .InputData1_RS(S), .InputData2_RT(multiplexer_5_out), .OutputData_RD(ALU_outputdata_rd),
    .shamt(shamt));  // open: ovf
  and and_1 (and_1_out, bne, zero_1_out_3);
  not not_3 (not_3_out, clk);
  Keyboard keyboard_1 (.clk(clk), .re(ioin), .clr(reset), .avail(keyboard_1_avail), .data(keyboard_1_data));
  Multiplexer #(.width(16), .enable("false")) multiplexer_6 (
    .in0(increment_result), .in1(adder_1_result), .out(multiplexer_6_out), .sel(and_1_out));
  RAM #(.addrWidth(16), .dataWidth(16), .bus("separate")) ram_1 (
    .addr(ALU_outputdata_rd), .din(registerfile_1_readdata2), .data(ram_1_data), .str(DMwe), .clk(not_3_out));  // open: sel, ld, clr
  Multiplexer #(.select(2), .width(16), .enable("false")) multiplexer_7 (
    .in0(multiplexer_6_out), .in1(address), .in2(S), .in3(address), .out(multiplexer_7_out), .sel(jump));
  Multiplexer #(.width(16), .enable("false")) multiplexer_8 (
    .in0(ALU_outputdata_rd), .in1(ram_1_data), .out(multiplexer_8_out), .sel(Rwd));
  \input  input_1 (.Data(keyboard_1_data), .in_2(keyboard_1_avail), .key(key));
endmodule

module zero (
  input  [15:0] \input ,
  input  blt,
  output out_3
);

  wire and_1_out, or_1_out, xor_1_out, xor_2_out, xor_3_out, xor_4_out, xor_5_out, xor_6_out, xor_7_out,
       xor_8_out, xor_9_out, xor_10_out, xor_11_out, xor_12_out, xor_13_out, xor_14_out, xor_15_out,
       xor_16_out;

  xor xor_1 (xor_1_out, 1'b0, \input [0]);
  xor xor_2 (xor_2_out, 1'b0, \input [1]);
  xor xor_3 (xor_3_out, 1'b0, \input [2]);
  xor xor_4 (xor_4_out, 1'b0, \input [3]);
  xor xor_5 (xor_5_out, 1'b0, \input [4]);
  xor xor_6 (xor_6_out, 1'b0, \input [5]);
  xor xor_7 (xor_7_out, 1'b0, \input [6]);
  xor xor_8 (xor_8_out, 1'b0, \input [7]);
  xor xor_9 (xor_9_out, 1'b0, \input [8]);
  xor xor_10 (xor_10_out, 1'b0, \input [9]);
  xor xor_11 (xor_11_out, 1'b0, \input [10]);
  xor xor_12 (xor_12_out, 1'b0, \input [11]);
  xor xor_13 (xor_13_out, 1'b0, \input [12]);
  xor xor_14 (xor_14_out, 1'b0, \input [13]);
  xor xor_15 (xor_15_out, 1'b0, \input [14]);
  xor xor_16 (xor_16_out, 1'b0, \input [15]);
  and and_1 (and_1_out, \input [15], 1'b1);
  or or_1 (or_1_out, xor_1_out, xor_2_out, xor_3_out, xor_4_out, xor_5_out, xor_6_out, xor_7_out, xor_8_out, xor_9_out, xor_10_out, xor_11_out, xor_12_out, xor_13_out, xor_14_out, xor_15_out, xor_16_out);
  Multiplexer #(.enable("false")) multiplexer_1 (.in0(or_1_out), .in1(and_1_out), .out(out_3), .sel(blt));
endmodule

module \input  (
  input  [6:0] Data,
  input  in_2,
  output [15:0] key
);

  Multiplexer #(.width(7), .enable("false")) multiplexer_1 (.in0({7{1'b0}}), .in1(Data), .out(key[6:0]), .sel(in_2));
  not not_1 (key[7], in_2);

  assign key[15:8] = {8{1'b0}};
endmodule
